// Digital circuit reg_file.dig as structural Verilog
module reg_file (
  input  [2:0] RS1,
  input  [2:0] RS2,
  input  [2:0] WS,
  input  WE,
  input  [15:0] IN,
  input  clk,
  output [15:0] OUT1,
  output [15:0] OUT2
);

  // NotConnected on OUT1
  // NotConnected on OUT2

  // Notes on the sheet:
  //   RS1: The index of the register which should output its value to OUT1.
  //   RS2: The index of the register which should output its value to OUT2.
  //   WS: The index of the register which should save the value on IN on the next clock cycle (if WE is high).
  //   WE: Whether the register selected by WS should save the value from IN on the next cycle.
  //   IN: The value to be saved into the register specified by WS if WE is high,
  //   OUT1: The value in the register specified by RS1.
  //   OUT2: The value in the register specified by RS2.
endmodule

/* Test case:
clk RS1 RS2 WS WE IN OUT1 OUT2
c 0 0 0 1 0x1234 0x1234 0x1234
c 1 0 1 1 0xBEEF 0xBEEF 0x1234
c 2 1 2 1 0xDEAD 0xDEAD 0xBEEF
c 3 2 3 1 0xFFFF 0xFFFF 0xDEAD
c 3 2 3 0 0xABCD 0xFFFF 0xDEAD
c 3 2 2 0 0xABCD 0xFFFF 0xDEAD
c 1 0 1 0 0xABCD 0xBEEF 0x1234
c 1 0 0 0 0xABCD 0xBEEF 0x1234
c 1 0 2 1 0xBADE 0xBEEF 0x1234
c 0 2 2 1 0xBADE 0x1234 0xBADE
c 0 0 2 0 0x1234 0x1234 0x1234
c 2 3 0 1 0x0000 0xBADE 0xFFFF
c 0 0 2 0 0x1234 0x0000 0x0000
*/
