// Digital circuit cpu.dig as structural Verilog
module cpu (
  input  CLK
);

  wire [15:0] PC_q, plus_1_s;

  Register #(.Bits(16), .isProgramCounter("true")) PC (.D(plus_1_s), .C(CLK), .en(1'b1), .Q(PC_q));
  Add #(.Bits(16)) plus_1 (.a(16'h1), .b(PC_q), .c_i(1'b0), .s(plus_1_s));  // open: c_o
  RAMDualAccess #(.AddrBits(16), .Bits(16)) RAM (.C(CLK), .A2(PC_q));  // open: str, ld, A1, Din1, D1, D2
endmodule
